// Logisim project CPU_t3.circ as structural Verilog
module main (
);

  wire CLK, cpu_1_p3, keyboard_1_avail, not_1_out, not_2_out, undriven;
  wire [23:0] cpu_1_p1;
  wire [31:0] cpu_1_p2;

  Clock clock_1 (.out(CLK));
  // CPU cpu_1: pin names not known; wires that end beside it: cpu_1_p1, cpu_1_p2, cpu_1_p3
  not not_1 (not_1_out, cpu_1_p3);
  Keyboard keyboard_1 (.clk(CLK), .re(cpu_1_p3), .clr(undriven), .avail(keyboard_1_avail), .data(cpu_1_p2[6:0]));
  RAM #(.addrWidth(20), .dataWidth(32)) ram_1 (
    .addr(cpu_1_p1[19:0]), .we(cpu_1_p3), .oe(not_1_out), .clk(CLK), .din(cpu_1_p2), .dout(cpu_1_p2));
  TTY #(.cols(120), .rows(48)) tty_1 ();  // open: data, clk, we, clr
  // Buzzer buzzer_1: pin names not known; wires that end beside it: cpu_1_p1, cpu_1_p2, cpu_1_p3, cpu_1_p2
  not not_2 (not_2_out, cpu_1_p3);
  RAM #(.addrWidth(16), .dataWidth(32)) ram_2 (
    .addr(cpu_1_p1[15:0]), .we(cpu_1_p3), .oe(not_2_out), .clk(CLK), .din(cpu_1_p2), .dout(cpu_1_p2));
  ROM #(.addrWidth(24), .dataWidth(32)) rom_1 (.addr(cpu_1_p1), .data(cpu_1_p2));
  // RGB_Video #(.height(256), .scale(8), .width(256)) rgb_video_1: pin names not known; wires that end beside it: CLK, cpu_1_p3, cpu_1_p2, cpu_1_p2, cpu_1_p2
  // Pins of 16 and 20 and 24 bits meet at cpu_1_p1
  // Pins of 7 and 32 bits meet at cpu_1_p2
endmodule

module CPU (
  output Address,
  output Data,
  output R_W
);

  ControlUnit controlunit_1 ();
  ALU alu_1 ();
  RegisterFile registerfile_1 ();
  Register InstructionRegister ();  // open: D, en, clk, Q, clr
  Register StackRegister ();  // open: D, en, clk, Q, clr
  Register AddressRegister ();  // open: D, en, clk, Q, clr
  Register MDR ();  // open: D, en, clk, Q, clr
endmodule
